// Logisim project Lab01_Mux21.circ as structural Verilog: 1 circuit, main circuit main
module main (
  input  Sel,
  input  In1,
  input  In2,
  output out
);

  wire and_1_out, and_2_out, not_1_out, not_2_out;

  not not_1 (not_1_out, Sel);
  not not_2 (not_2_out, not_1_out);
  and and_1 (and_1_out, not_2_out, In1);
  and and_2 (and_2_out, not_1_out, In2);
  or or_1 (out, and_1_out, and_2_out);

  // Notes on the sheet:
  //   Lab1_Dinmukhamed Sailau_2to1Mux_14.02.25
endmodule
