// Logisim project Lab02_Bool.circ as structural Verilog: 3 circuits, main circuit main
module main (
  input  A,
  input  B,
  input  C,
  input  in_4,
  input  in_5,
  input  in_6,
  input  in_7,
  output Out,
  output out_9
);

  Equation_1 equation_1_1 (.A1(A), .B1(B), .C1(C), .True1(Out));
  Equation_2 equation_2_1 (.A2(in_4), .B2(in_5), .C2(in_6), .D2(in_7), .True2(out_9));

  // Notes on the sheet:
  //   Dinmukhamed_Lab02_14.02.25
endmodule

module Equation_2 (
  input  A2,
  input  B2,
  input  C2,
  input  D2,
  output True2
);

  wire and_1_out, and_2_out, and_3_out, and_4_out;

  and and_1 (and_1_out, ~A2, ~B2, C2, ~D2);  // AND_Gate
  and and_2 (and_2_out, ~A2, B2, C2, D2);  // AND_Gate
  and and_3 (and_3_out, A2, ~B2, C2, ~D2);  // AND_Gate
  and and_4 (and_4_out, A2, B2, C2, ~D2);  // AND_Gate
  or or_1 (True2, and_1_out, and_2_out, and_3_out, and_4_out);

  // Notes on the sheet:
  //   (A'B'CD')+(A'BCD)+(AB'CD')+(ABCD')
endmodule

module Equation_1 (
  input  A1,
  input  B1,
  input  C1,
  output True1
);

  wire and_1_out, and_2_out, and_3_out;

  and and_1 (and_1_out, ~A1, B1, ~C1);  // AND_Gate
  and and_2 (and_2_out, ~A1, ~B1, C1);  // AND_Gate
  and and_3 (and_3_out, A1, B1, C1);
  or or_1 (True1, and_1_out, and_2_out, and_3_out);

  // Notes on the sheet:
  //   (A'BC')+(AB'C')+(ABC)
endmodule
